# Fritzing sketch PiZeroC64 r10 (saved by Fritzing 0.9.3b)
circuit board: 5.66027cm x 7.73427cm
breadboards: 1

parts:
  1 = Pad [width=3.03585894193728 height=6.87308646450179 connect=center]
  Reset = Pushbutton [package="[THT]"]
  1_2 = single row smd female pin header, 1 pin [form="♀ (female)"]
  2 = single row smd female pin header, 1 pin [form="♀ (female)"]
  3 = single row smd female pin header, 1 pin [form="♀ (female)"]
  12 = single row smd female pin header, 1 pin [form="♀ (female)"]
  3_2 = Pad [width=3.03585894193728 height=6.87308646450179 connect=center]
  4 = Pad [width=3.03585894193728 height=6.87308646450179 connect=center]  # not connected
  2_2 = Pad [width=3.03585894193728 height=6.87308646450179 connect=center]
  5 = Pad [width=3.03585894193728 height=6.87308646450179 connect=center]  # not connected
  6 = Pad [width=3.03585894193728 height=6.87308646450179 connect=center]
  7 = Pad [width=3.03585894193728 height=6.87308646450179 connect=center]  # not connected
  8 = Pad [width=3.03585894193728 height=6.87308646450179 connect=center]  # not connected
  9 = Pad [width=3.03585894193728 height=6.87308646450179 connect=center]  # not connected
  10 = Pad [width=3.03585894193728 height=6.87308646450179 connect=center]  # not connected
  11 = Pad [width=3.03585894193728 height=6.87308646450179 connect=center]  # not connected
  12_2 = Pad [width=3.03585894193728 height=6.87308646450179 connect=center]
  N = Pad [width=3.03585894193728 height=6.87308646450179 connect=center]
  B = Pad [width=3.03585894193728 height=6.87308646450179 connect=center]
  C = Pad [width=3.03585894193728 height=6.87308646450179 connect=center]
  D = Pad [width=3.03585894193728 height=6.87308646450179 connect=center]
  E = Pad [width=3.03585894193728 height=6.87308646450179 connect=center]
  F = Pad [width=3.03585894193728 height=6.87308646450179 connect=center]
  H = Pad [width=3.03585894193728 height=6.87308646450179 connect=center]
  J = Pad [width=3.03585894193728 height=6.87308646450179 connect=center]
  K = Pad [width=3.03585894193728 height=6.87308646450179 connect=center]
  L = Pad [width=3.03585894193728 height=6.87308646450179 connect=center]
  M = Pad [width=3.03585894193728 height=6.87308646450179 connect=center]
  D_2 = single row smd female pin header, 1 pin [form="♀ (female)"]
  M_2 = single row smd female pin header, 1 pin [form="♀ (female)"]
  A = single row smd female pin header, 1 pin [form="♀ (female)"]
  H_2 = single row smd female pin header, 1 pin [form="♀ (female)"]
  F_2 = single row smd female pin header, 1 pin [form="♀ (female)"]
  C_2 = single row smd female pin header, 1 pin [form="♀ (female)"]
  Reset_2 = Pushbutton [package="[THT]"]
  E_2 = single row smd female pin header, 1 pin [form="♀ (female)"]
  L_2 = single row smd female pin header, 1 pin [form="♀ (female)"]
  B_2 = single row smd female pin header, 1 pin [form="♀ (female)"]
  J_2 = single row smd female pin header, 1 pin [form="♀ (female)"]
  K_2 = single row smd female pin header, 1 pin [form="♀ (female)"]
  N_2 = single row smd female pin header, 1 pin [form="♀ (female)"]
  A_2 = Pad [width=3.03585894193728 height=6.87308646450179 connect=center]  # not connected
  Pad1 = Pad [width=5.22210362219904 height=1.7 connect=center]  # not connected
  UP9600 = male pin header, 2 pins [form="♂ (male)"]
  5_2 = single row smd female pin header, 1 pin [form="♀ (female)"]
  6_2 = single row smd female pin header, 1 pin [form="♀ (female)"]
  7_2 = single row smd female pin header, 1 pin [form="♀ (female)"]
  UP5V = male pin header, 2 pins [form="♂ (male)"]
  UP9600-5 = male pin header, 2 pins [form="♂ (male)"]
  Video = RCA [package=rca_lock]
  TV = female pin header, 2 pins [form="♀ (female)"]
  Run = female pin header, 2 pins [form="♀ (female)"]
  U1 = IC, DIP package, 20 pins [chip_label=75HC245]
  Raspberry_Pi_Zero2_(Fixed) = Raspberry Pi Zero
  C5V = Capacitor Polarized [package=cpol-radial-10uf-25v]

nets:
  GND: 1.pad, 1_2.pin1, 12.pin1, 12_2.pad, N.pad, A.pin1, Reset_2.Pin_3, Reset_2.Pin_4, N_2.pin1, U1.pin10, U1.pin19, Raspberry_Pi_Zero2_(Fixed).GND, C5V.-
  N1: Reset.Pin_1, Reset.Pin_2, Run.pin2
  N2: Reset.Pin_3, Reset.Pin_4, Run.pin1
  N3: 2.pin1, 2_2.pad, UP5V.pin2
  N4: 3.pin1, 3_2.pad, Reset_2.Pin_1, Reset_2.Pin_2
  N5: 6.pad, UP9600.pin1, 6_2.pin1
  RxD_64: B.pad, C.pad, C_2.pin1, B_2.pin1, 7_2.pin1, U1.pin18
  N6: D.pad, D_2.pin1
  N7: E.pad, E_2.pin1
  N8: F.pad, F_2.pin1
  N9: H.pad, H_2.pin1
  N10: J.pad, J_2.pin1
  N11: K.pad, K_2.pin1
  N12: L.pad, L_2.pin1, UP9600.pin2
  TxD_64: M.pad, M_2.pin1, UP9600-5.pin1, U1.pin3
  N13: 5_2.pin1, UP9600-5.pin2
  5V: UP5V.pin1, Raspberry_Pi_Zero2_(Fixed).5V, C5V.+
  N14: Video.PIN, TV.pin1
  N15: Video.SHELL, TV.pin2
  3.3V: U1.pin1, U1.pin20, Raspberry_Pi_Zero2_(Fixed).3v3, Raspberry_Pi_Zero2_(Fixed).3V3
  TxD_Pi: U1.pin2, Raspberry_Pi_Zero2_(Fixed).GPIO14
  RxD_Pi: U1.pin17, Raspberry_Pi_Zero2_(Fixed).GPIO15

notes:
  Actual C64 User Port
  Pi
  Assumptions:
  C64 5V is clean/stable enough to use as 5V VIN directly
  C64
  Other Side Up!
  Jumper to disconnect 5V from User Port
  Connections through 74HC245:
  TxD_Pi -> RxD_64 (A1 -> B1) Data from Pi to 64
  TxD_64 -> RxD_Pi (A2 -> B2) Data from 64 to Pi
  Pi is 3.3V, C64 is 5V
  Out
  Raspberry Pi Zero W
  Version 0.1
  Leif Bloomquist 2017
  Commodore 64 Interface
  TM

custom parts:
  Raspberry Pi Zero: The Raspberry Pi Zero is half the size of a Model A+, with twice the utility. A tiny Raspberry Pi that’s affordable enough for any project! · 1Ghz, Single-core CPU · 512MB RAM · Mini HDMI and USB On-The-Go ports · Micro USB power · HAT-compatible 40-pin header. In this version schematic has been changed so the pins match the GPIO connector. I.e. the left hand pins are all the pins (the power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
